# Fritzing sketch Esquema02 (saved by Fritzing 0.9.3b)
perfboards: 1

parts:
  Componente1 = Arduino Nano (Rev3.0)
  J1 = Screw terminal - 2 pins [package=THT]
  R1 = Resistor [tolerance=±5% resistance=10k package=THT]
  Sensor_de_fuerza = Basic Force Sensing Resistor (FSR) [package=THT]
  R2-P_umbral = Rotary Potentiometer (Small) [maximum_resistance=10kΩ package=THT]
  R3 = Resistor [tolerance=±5% resistance=1k package=THT]
  Q1-Transistor = NPN-Transistor [package="TO92 [THT]"]
  R4 = Resistor [tolerance=±5% resistance=1k package=THT]
  LED_Rojo = LED - 5mm [color="Red (633nm)" package="5 mm [THT]"]
  J2 = Screw terminal - 2 pins [package=THT]
  D1 = Rectifier Diode [part_number=1N4001 package="300 mil [THT]"]
  VCC1 = Battery
  J3 = Screw terminal - 2 pins [package=THT]
  Motor-Vibrador = Microphone

nets:
  GND: Componente1.GND, R1.Pin_1, R2-P_umbral.leg1, Q1-Transistor.E, LED_Rojo.cathode, VCC1.-, J3.pin2
  N1: Componente1.D3, R3.Pin_0
  N2: Componente1.VIN, J2.pin2, D1.cathode, VCC1.+, J3.pin1, Motor-Vibrador.pin2
  N3: Componente1.5V, J1.pin1, Sensor_de_fuerza.pin_0, R2-P_umbral.leg2
  N4: Componente1.A2, J1.pin2, R1.Pin_0, Sensor_de_fuerza.pin_1
  N5: Componente1.A0, R2-P_umbral.wiper
  N6: R3.Pin_1, Q1-Transistor.B
  N7: Q1-Transistor.C, R4.Pin_1, J2.pin1, D1.anode, Motor-Vibrador.pin1
  N8: R4.Pin_0, LED_Rojo.anode

notes:
  Mecano-Amplificador, Mª Teresa Aliaga Vega                                                                  Manuel Hidalgo Diaz
